# Fritzing sketch www-server-hardware-02 (saved by Fritzing 0.9.3b)
breadboards: 1

parts:
  Part1 = Lithium Ion Polymer Battery 3.7v 2500mAh [part_number=328]  # not connected
  Part2 = Adafruit USB DC Solar LiPo Charger [part_number="Adafruit #390"]
  Part3 = Adafruit Feather HUZZAH ESP8266 [part_number="Adafruit #2821"]
  U1 = attiny85 [package=dip]
  R1 = Resistor [tolerance=±5% resistance=330 package=THT]
  LED1 = LED - 5mm [color="Red (633nm)" package="5 mm [THT]"]

nets:
  GND: Part2.GND, Part3.GND, U1.Pin_4, LED1.cathode
  N1: Part2.LOAD, Part3.VBAT, U1.Pin_8
  N2: Part3.CH_PD, U1.Pin_2
  N3: Part3.GPIO13/MOSI, U1.Pin_5
  N4: Part3.RESET, U1.Pin_7
  N5: U1.Pin_3, R1.Pin_1
  N6: R1.Pin_0, LED1.anode

custom parts:
  Lithium Ion Polymer Battery 3.7v 2500mAh: Lithium ion polymer (also known as 'lipo' or 'lipoly') batteries are thin, light and powerful. The output ranges from 4.2V when completely charged to 3.7V. This battery has a capacity of 2500mAh for a total of about 10 Wh. The batteries come pre-attached with a genuine 2-pin JST-PH connector as shown and include the necessary protection circuitry.
  Adafruit USB DC Solar LiPo Charger: Make your projects to go green this summer with our specialized USB/Solar Lithium Ion Polymer Battery charger! This charger is a very unique design, perfect for outdoor projects, or DIY iPod chargers. We've spent over a year testing and tinkering with this charger to come up with a plug and play solution to charging batteries with the sun and we're really pleased with what we ended up with.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
  Adafruit Feather HUZZAH ESP8266: his is the Adafruit Feather HUZZAH ESP8266 - our take on an 'all-in-one' ESP8266 WiFi development board with built in USB and battery charging. Its an ESP8266 WiFi module with all the extras you need, ready to rock! We have other boards in the Feather family, check'em out here. At the Feather HUZZAH's heart is an ESP8266 WiFi microcontroller clocked at 80 MHz and at 3.3V logic. This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
